# Fritzing sketch Sketch (saved by Fritzing 0.9.3b)
breadboards: 1

parts:
  M1 = DOIT Esp32 DevKit v1 (30 pins long, 11 pins width) [part_number=ESP32S-PIN30]
  Componente1 = RTC DS3231
  TCRT1 = TCRT5000 sensor module [part_number=151608]
  VCC1 = 4 x AAA Battery Mount

nets:
  3V3: M1.3V3, Componente1.VCC, TCRT1.D+, VCC1.+
  GND: M1.GND, Componente1.GND, TCRT1.D-, VCC1.-
  N1: M1.D15, TCRT1.T+
  N2: M1.D21, Componente1.SDA
  N3: M1.D22, Componente1.SCL

custom parts:
  DOIT Esp32 DevKit v1 (30 pins long, 11 pins width): The DOIT Esp32 DevKit v1 is one of the development board created by DOIT to evaluate the ESP-WROOM-32 module. It is based on the ESP32 microcontroller that boasts Wifi, Bluetooth, Ethernet and Low Power support all in a single chip. (vanepp) made breadboard work, adjusted pin numbering and labels and reduced size of schematic and cleaned up pcb. This chip is 30pins long (2 x15) and 11 pins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
  RTC DS3231: DS3231 with akku
  TCRT5000 sensor module: breakout board with TCRT5000
